// Logisim project T2比较器.circ as structural Verilog: 1 circuit, main circuit main
module main (
  input  B,
  input  A,
  output F1,
  output F2,
  output F3
);

  wire not_1_out, not_2_out;

  not not_1 (not_1_out, B);
  not not_2 (not_2_out, A);
  and and_1 (F1, not_1_out, A);
  and and_2 (F3, B, not_2_out);
  nor nor_1 (F2, F1, F3);
endmodule
